// Logisim project HW8.circ as structural Verilog: 1 circuit, main circuit main
module main (
  input  I,
  output L
);

  wire and_1_out, and_2_out, and_3_out, CLK_out, d_ff_1_q, d_ff_1_qn, d_ff_2_q, d_ff_2_qn, not_1_out,
       or_1_out;

  Clock CLK (.out(CLK_out));
  not not_1 (not_1_out, I);
  and and_1 (and_1_out, d_ff_1_q, d_ff_2_qn);
  and and_2 (and_2_out, d_ff_1_q, I);
  and and_3 (and_3_out, not_1_out, d_ff_2_q, d_ff_1_qn);
  or or_1 (or_1_out, and_1_out, and_2_out, and_3_out);
  D_Flip_Flop d_ff_1 (.clk(or_1_out), .D(CLK_out), .Q(d_ff_1_q), .Qn(d_ff_1_qn));  // open: preset, en, reset
  D_Flip_Flop d_ff_2 (.clk(I), .D(CLK_out), .Q(d_ff_2_q), .Qn(d_ff_2_qn));  // open: preset, en, reset
  xor xor_1 (L, d_ff_1_q, d_ff_2_q);
endmodule
